# Fritzing sketch sketch (saved by Fritzing 0.9.2b)
breadboards: 1

parts:
  Part1 = Arduino Uno (Rev3) - ICSP
  R1 = Resistor [tolerance=±5% resistance=330 package="1206 [SMD]"]
  R2 = Resistor [tolerance=±5% resistance=330 package="1206 [SMD]"]
  R3 = Resistor [tolerance=±5% resistance=220 package="1206 [SMD]"]
  R4 = Resistor [tolerance=±5% resistance=220 package="1206 [SMD]"]
  R5 = Resistor [tolerance=±5% resistance=330 package="1206 [SMD]"]
  LED1 = smd LED [color="Red (633nm)" package="0603 [SMD]"]
  Part2 = Bluetooth HC-06

nets:
  N1: Part1.D8, R5.Pin_1
  N2: Part1.D0/RX, Part2.TXD
  N3: Part1.D1/TX, R1.Pin_0
  5V: Part1.5V, Part2.VCC
  GND: Part1.GND, R4.Pin_1, LED1.anode, Part2.GND
  N4: R1.Pin_1, R2.Pin_0
  N5: R2.Pin_1, R3.Pin_1, Part2.RXD
  N6: R3.Pin_0, R4.Pin_0
  N7: R5.Pin_0, LED1.cathode
