# Fritzing sketch sketch (saved by Fritzing 0.9.2b)
breadboards: 1

parts:
  Part1 = Arduino Uno (Rev3) - ICSP
  R1 = Resistor [tolerance=±5% resistance=330 package="1206 [SMD]"]
  R2 = Resistor [tolerance=±5% resistance=330 package="1206 [SMD]"]
  R3 = Resistor [tolerance=±5% resistance=220 package="1206 [SMD]"]
  R4 = Resistor [tolerance=±5% resistance=220 package="1206 [SMD]"]
  Part2 = Bluetooth HC-06
  T1 = LM35 Temperature Sensor [package="TO92 [THT]"]

nets:
  N1: Part1.A0, T1.Vout
  N2: Part1.D0/RX, Part2.TXD
  N3: Part1.D1/TX, R1.Pin_0
  5V: Part1.5V, Part2.VCC, T1.+Vs
  GND: Part1.GND, R4.Pin_1, Part2.GND, T1.GND
  N4: R1.Pin_1, R2.Pin_0
  N5: R2.Pin_1, R3.Pin_1, Part2.RXD
  N6: R3.Pin_0, R4.Pin_0
