# Fritzing sketch sketch (saved by Fritzing 0.9.2b)
breadboards: 1

parts:
  Part1 = Arduino Uno (Rev3) - ICSP
  R3 = Resistor [tolerance=±5% resistance=10k package="1206 [SMD]"]
  R4 = PHOTOCELL [package=photocell]  # not connected

nets:
  N1: Part1.A1, R3.Pin_1
  N2: Part1.GND, R3.Pin_0
