# Fritzing sketch sketch (saved by Fritzing 0.9.2b)
breadboards: 1

parts:
  R1 = Resistor [tolerance=±5% resistance=330 package="2010 [SMD]"]
  R2 = Resistor [tolerance=±5% resistance=330 package="2010 [SMD]"]
  R3 = Resistor [tolerance=±5% resistance=330 package="2010 [SMD]"]
  Part1 = Arduino Uno (Rev3)
  LED1 = RGB LED (com. cathode, rbg) [package="5 mm [THT]"]  # not connected

nets:
  N1: R1.Pin_1, Part1.D11_PWM/MOSI
  N2: R2.Pin_1, Part1.D10_PWM/SS
  N3: R3.Pin_1, Part1.D9_PWM
