# Fritzing sketch layout (saved by Fritzing 0.9.2b)
breadboards: 1

parts:
  Part1 = Arduino Uno (Rev3)
  T1 = LM35 Temperature Sensor [package="TO92 [THT]"]
  LED1 = LED - 5mm [color="Red (633nm)" package="5 mm [THT]"]
  R1 = Resistor [tolerance=±5% resistance=220 package=THT]

nets:
  N1: Part1.A0, T1.Vout
  N2: Part1.D10_PWM/SS, R1.Pin_1
  N3: Part1.5V, T1.+Vs
  GND: Part1.GND, T1.GND, LED1.cathode
  N4: LED1.anode, R1.Pin_0
